# Fritzing sketch keypad (saved by Fritzing 0.9.0b)
circuit board: 8.46667cm x 5.64444cm
breadboards: 1

parts:
  KEYPAD1 = Membrane Matrix Keypad
  Adafruit_Bluefruit_HID1 = Adafruit Bluefruit Bluetooth Module
  VCC1 = Battery block 9V
  U1 = atmega328 [package=dip]

nets:
  N1: KEYPAD1.1, U1.D8
  N2: KEYPAD1.2, U1.D7
  N3: KEYPAD1.3, U1.D6_(PWM)
  N4: KEYPAD1.4, U1.D5_(PWM)
  N5: KEYPAD1.5, U1.D4
  N6: KEYPAD1.6, U1.D3_(PWM)
  N7: KEYPAD1.7, U1.D2
  N8: Adafruit_Bluefruit_HID1.RX, U1.D1_(TX)
  N9: Adafruit_Bluefruit_HID1.3v, U1.VCC, U1.AVCC
  N10: Adafruit_Bluefruit_HID1.Vin, VCC1.+
  N11: Adafruit_Bluefruit_HID1.Ground#10, VCC1.-
  N12: Adafruit_Bluefruit_HID1.Ground#11, U1.GND

custom parts:
  Membrane Matrix Keypad: Membrane Matrix 3x4 Keypad
